// Logisim project NOR.circ as structural Verilog: 1 circuit, main circuit main
module main (
  input  X,
  input  Y,
  output out_3,
  output out_4,
  output out_5,
  output out_6
);

  wire nor_1_out, nor_2_out, nor_3_out, nor_4_out, nor_5_out, nor_6_out, nor_9_out, nor_10_out, nor_11_out,
       nor_12_out;

  nor nor_1 (nor_1_out, X, X);
  nor nor_2 (nor_2_out, Y, Y);
  nor nor_3 (nor_3_out, X, Y);
  nor nor_4 (nor_4_out, X, X);
  nor nor_5 (nor_5_out, Y, Y);
  nor nor_6 (nor_6_out, X, Y);
  nor nor_7 (out_3, nor_1_out, nor_2_out);
  nor nor_8 (out_4, nor_3_out, nor_3_out);
  nor nor_9 (nor_9_out, nor_4_out, nor_5_out);
  nor nor_10 (nor_10_out, X, Y);
  nor nor_11 (nor_11_out, X, nor_6_out);
  nor nor_12 (nor_12_out, nor_6_out, Y);
  nor nor_13 (out_5, nor_9_out, nor_10_out);
  nor nor_14 (out_6, nor_11_out, nor_12_out);

  // Notes on the sheet:
  //   AND from NOR Gates
  //   OR from NOR Gates
  //   XOR from NOR Gates
  //   XNOR from NOR Gates
endmodule
